// Logisim project AutomatedRAM.circ as structural Verilog: 1 circuit, main circuit main
module main (
);

  wire clock_1_out, clock_2_out;
  wire [7:0] ram_1_data, random_1_out;
  wire [15:0] counter_1_q;

  Clock #(.highDuration(2), .lowDuration(2)) clock_1 (.out(clock_1_out));
  Counter #(.width(16), .max('hffff)) counter_1 (
    .count(1'b1), .Q(counter_1_q), .clk(clock_1_out), .clr(1'b0));  // open: load, D, carry
  Random random_1 (.clk(clock_1_out), .next(1'b1), .out(random_1_out), .clr(1'b0));
  Clock clock_2 (.out(clock_2_out));
  RAM #(.addrWidth(16), .bus("separate")) ram_1 (
    .addr(counter_1_q), .din(random_1_out), .data(ram_1_data), .sel(1'b1), .clk(clock_2_out));  // open: str, ld, clr
  Hex_Digit_Display hex_digit_display_1 (.value(ram_1_data[3:0]));  // open: dp
  Hex_Digit_Display hex_digit_display_2 (.value(ram_1_data[7:4]));  // open: dp
endmodule
